# Fritzing sketch Schematics (saved by Fritzing 0.9.3b)
perfboards: 3

parts:
  R6 = Resistor [tolerance=±5% resistance=220 package=THT]
  LED6 = LED - 5mm [color="Red (633nm)" package="5 mm [THT]"]
  R9 = Resistor [tolerance=±5% resistance=220 package=THT]
  LED9 = LED - 5mm [color="Red (633nm)" package="5 mm [THT]"]
  LED7 = LED - 5mm [color="Red (633nm)" package="5 mm [THT]"]
  J1 = Camdenboss CTB0158-2 [part_number=CTB0158-2 package=THT]
  Raspberry_Pi_2 = Raspberry Pi 3 [part_number=RPI-3-V1.2]
  Power_plug1 = Power plug
  LED4 = LED - 5mm [color="Red (633nm)" package="5 mm [THT]"]
  R8 = Resistor [tolerance=±5% resistance=220 package=THT]  # not connected
  Q2 = TRANSISTOR_NPN [package=to-92]
  LED5 = LED - 5mm [color="Red (633nm)" package="5 mm [THT]"]
  LED8 = LED - 5mm [color="Red (633nm)" package="5 mm [THT]"]
  R5 = Resistor [tolerance=±5% resistance=220 package=THT]  # not connected
  R7 = Resistor [tolerance=±5% resistance=220 package=THT]  # not connected
  R4 = Resistor [tolerance=±5% resistance=220 package=THT]  # not connected

nets:
  N1: R6.Pin_0, LED6.cathode
  N2: R9.Pin_0, LED9.cathode
  N3: LED7.cathode, LED8.cathode
  N4: J1.pin2, Raspberry_Pi_2.GPIO3, Raspberry_Pi_2.GND, Q2.E
  N5: J1.terminal_1, Power_plug1.VCC
  N6: J1.terminal_2, Power_plug1.GND
  N7: Raspberry_Pi_2.GPIO4, Q2.C
  N8: LED4.cathode, LED5.cathode
